# Fritzing sketch transmitter (saved by Fritzing 0.9.3b)
breadboards: 2

parts:
  Part1 = Arduino Uno (Rev3)
  HC-SR04_Sensor_1 = HC-SR04 Ultrasonic Distance Sensor
  S1 = Pushbutton [package="[THT]"]
  X2 = X113647 Stepper Driver Board [part_number=X113647 package=board]
  MOTOR4 = 28BYJ-48 Stepper Motor
  R1 = Resistor [tolerance=±5% resistance=10k package="0805 [SMD]"]

nets:
  N1: Part1.D8, X2.IN1
  N2: Part1.D9_PWM, X2.IN3
  N3: Part1.D10_PWM/SS, X2.IN2
  N4: Part1.D11_PWM/MOSI, X2.IN4
  N5: Part1.D2, HC-SR04_Sensor_1.TRIG
  N6: Part1.D3_PWM, HC-SR04_Sensor_1.ECHO
  N7: Part1.D4, S1.Pin_1, S1.Pin_2, R1.Pin_0
  5V: Part1.5V, HC-SR04_Sensor_1.VCC, S1.Pin_3, S1.Pin_4, X2.+V
  GND: Part1.GND, HC-SR04_Sensor_1.GND, X2.GND, R1.Pin_1
  N8: X2.BLUE, MOTOR4.BLUE
  N9: X2.PINK, MOTOR4.PINK
  N10: X2.YELLOW, MOTOR4.YELLOW
  N11: X2.ORANGE, MOTOR4.ORANGE
  N12: X2.RED, MOTOR4.RED

custom parts:
  HC-SR04 Ultrasonic Distance Sensor: The HC-SR04 is an ultrasonic distance sensor. It is capable of providing measurement for ranges of 2cm to 400cm. The module operates at 5V.
  X113647 Stepper Driver Board: A common stepper motor driver board based on ULN2003APG darlington array
  28BYJ-48 Stepper Motor: 28BYJ-48 gear-reduction stepper motor (small)
